# Fritzing sketch DHT 11 Sketch  (saved by Fritzing 0.9.3b)

parts:
  Part1 = Arduino Uno (Rev3) - ICSP
  Mod1 = KY-015 Temperature & Humidity Sensor Module [package="Breakout board"]

nets:
  N1: Part1.D3_PWM, Mod1.S
  5V: Part1.5V, Mod1.Vin
  N2: Part1.GND, Mod1.-

custom parts:
  KY-015 Temperature & Humidity Sensor Module: KY-015 temperature and humidity sensor module, provides a low-latency serial interface to measure humidity and temperature.
